# Fritzing sketch montage (saved by Fritzing 0.9.9b)

parts:
  Part1 = Arduino Uno (Rev3)
  Part2 = Base Shield V2
  U1 = 4-Channel 5v Relay Shield [package=relay-4ch5v10a]  # not connected

nets:
  N1: Part1.A0, Part2.A0
  N2: Part1.A1, Part2.A1
  N3: Part1.A2, Part2.A2
  N4: Part1.A3, Part2.A3
  N5: Part1.A4/SDA, Part2.A4
  N6: Part1.A5/SCL, Part2.A5
  N7: Part1.D8, Part2.D8
  N8: Part1.D9_PWM, Part2.D9
  N9: Part1.D10_PWM/SS, Part2.D10
  N10: Part1.D11_PWM/MOSI, Part2.D11
  N11: Part1.D12/MISO, Part2.D12
  N12: Part1.D13/SCK, Part2.D13
  GND: Part1.GND, Part2.GND
  N13: Part1.AREF, Part2.AREF
  N14: Part1.D0/RX, Part2.D0/RX
  N15: Part1.D1/TX, Part2.D1/TX
  N16: Part1.D2, Part2.D2
  N17: Part1.D3_PWM, Part2.D3
  N18: Part1.D4, Part2.D4
  N19: Part1.D5_PWM, Part2.D5
  N20: Part1.D6_PWM, Part2.D6_PWM
  N21: Part1.D7, Part2.D7
  N22: Part1.ioref, Part2.ioref
  N23: Part1.RESET, Part2.RESET
  3V3: Part1.3V3, Part2.3V3
  5V: Part1.5V, Part2.5V
  VIN: Part1.VIN, Part2.VIN
  N24: Part1.N/C, Part2.N/C

custom parts:
  4-Channel 5v Relay Shield: 4 Channel 5v Relay Shield w. 2x SPD-06VDC-SD-C
